# Fritzing sketch Schemat (saved by Fritzing 0.9.4)

parts:
  R1 = Resistor [tolerance=±5% resistance=4.7k package=THT]
  Arduino = Arduino Nano (Rev3.0)
  DS18B20_1 = TEMPERATURE-SENSOR [package=to-92]
  DS18B20_2 = TEMPERATURE-SENSOR [package=to-92]
  DS18B20_15 = TEMPERATURE-SENSOR [package=to-92]
  Moduł_Peltiera_TEC12710 = Peltier Element
  9-16V = BANANA_CONN [package=banana_conn]
  GND = BANANA_CONN [package=banana_conn]
  Czujnik_temp_otoczenia = TEMPERATURE-SENSOR [package=to-92]
  Czujnik_zimnej_strony = TEMPERATURE-SENSOR [package=to-92]
  GND_2 = BANANA_CONN [package=banana_conn]
  9-16V_2 = BANANA_CONN [package=banana_conn]
  GND_3 = BANANA_CONN [package=banana_conn]
  DATA = BANANA_CONN [package=banana_conn]
  VCC = BANANA_CONN [package=banana_conn]
  VCC_2 = BANANA_CONN [package=banana_conn]
  DATA_2 = BANANA_CONN [package=banana_conn]
  GND_4 = BANANA_CONN [package=banana_conn]

nets:
  VCC: R1.Pin_0, Arduino.5V, DS18B20_1.VCC, Czujnik_temp_otoczenia.VCC, Czujnik_zimnej_strony.VCC, VCC.1, VCC_2.1
  N1: R1.Pin_1, Arduino.D10, DS18B20_1.ADJ, DS18B20_2.ADJ, DS18B20_15.ADJ, Czujnik_temp_otoczenia.ADJ, Czujnik_zimnej_strony.ADJ, DATA.1, DATA_2.1
  GND: Arduino.GND, DS18B20_1.GND, DS18B20_2.GND, DS18B20_15.GND, Czujnik_temp_otoczenia.GND, Czujnik_zimnej_strony.GND, GND_3.1, GND_4.1
  VCC_2: DS18B20_2.VCC, DS18B20_15.VCC
  N2: Moduł_Peltiera_TEC12710.pin1, GND.1, GND_2.1
  N3: Moduł_Peltiera_TEC12710.pin2, 9-16V.1, 9-16V_2.1

notes:
  .
  MES i MEB, Układ pomiarowy, 1
